# Fritzing sketch game-platform (saved by Fritzing 0.9.3b)
breadboards: 1

parts:
  Squix1 = OLED 0.96" 128x64 I2C SSD1306
  S1 = Pushbutton [package="[SMD]"]
  S2 = Pushbutton [package="[SMD]"]
  Part1 = Arduino Uno (Rev3)
  J1 = Piezo Speaker

nets:
  VCC: Squix1.VCC, Part1.5V
  GND: Squix1.GND, S1.Pin_3, S1.Pin_4, S2.Pin_1, S2.Pin_2, Part1.GND, J1.pin1
  N1: Squix1.SCL, Part1.A5/SCL
  N2: Squix1.SCA, Part1.A4/SDA
  N3: S1.Pin_1, S1.Pin_2, Part1.D2
  N4: S2.Pin_3, S2.Pin_4, Part1.D3_PWM
  N5: Part1.D6_PWM, J1.pin2
